# Fritzing sketch flush (saved by Fritzing 0.9.3b)
circuit board: 8.46667cm x 5.64444cm

parts:
  Part1 = Arduino Uno (Rev3)
  J1 = Basic Servo
  3-pins_Hall_Effect_Sensor1 = mystery part, 3 pins [chip_label="Hall Effect Sensor"]

nets:
  N1: Part1.D9_PWM, J1.pulse
  GND: Part1.GND, J1.gnd, 3-pins_Hall_Effect_Sensor1.pin1
  N2: Part1.D2, 3-pins_Hall_Effect_Sensor1.pin2
  5V: Part1.5V, J1.vcc, 3-pins_Hall_Effect_Sensor1.pin3
